# Fritzing sketch iot_proj (saved by Fritzing 0.9.3b)
breadboards: 1

parts:
  Part1 = Arduino Uno (Rev3)
  RHT1 = Humidity and Temperature Sensor RHT03
  Part2 = Soil Moisture Sensor

nets:
  N1: Part1.A0, Part2.SIG
  GND: Part1.GND, RHT1.GND_2, Part2.GND
  N2: Part1.D3_PWM, RHT1.Data-signal
  VCC: Part1.3V3, RHT1.Vcc, Part2.VCC

notes:
  water flow sensor
